# Fritzing sketch Complete_thermocycler (saved by Fritzing 0.9.3b)
breadboards: 1

parts:
  Part1 = Arduino Uno (Rev3)
  Q1 = Basic FET N-Channel [package="TO220 [THT]"]
  Q3 = Basic FET N-Channel [package="TO220 [THT]"]
  DS2 = DS18B20 1-Wire Temperature Sensor [part_number=DS18B20]
  R3 = Rotary Potentiometer (Small) [maximum_resistance=100kΩ package=THT]
  S3 = Pushbutton [package="[THT]"]
  Q2 = Basic FET N-Channel [package="TO220 [THT]"]
  R7 = Resistor [tolerance=±5% resistance=10k package=THT]
  R8 = Resistor [tolerance=±5% resistance=10k package=THT]
  R9 = Resistor [tolerance=±5% resistance=10k package=THT]
  D1 = Rectifier Diode [part_number=1N4001 package="Melf DO-213 AB [SMD]"]
  DS3 = DS18B20 1-Wire Temperature Sensor [part_number=DS18B20]
  M4 = DC Motor
  J4 = Power Jack [package=power_jack_smd]
  U3 = SWITCH-SPST-2 [package=r_sw_th]
  LCM1602_IIC3 = LCM1602 IIC [part_number="LCM1602 IIC" chip_label="LCM1602 IIC" package="DIP (Dual Inline) [THT]"]
  LCD2 = LCD screen
  R15 = Resistor [tolerance=±5% resistance=4.7k package=THT]
  R16 = Resistor [tolerance=±5% resistance=220 package="2512 [SMD]"]
  R17 = Resistor [tolerance=±5% resistance=220 package="2512 [SMD]"]
  R18 = Resistor [tolerance=±5% resistance=4.7k package=THT]
  R19 = Resistor [tolerance=±5% resistance=10k package=THT]

nets:
  N1: Part1.A4/SDA, LCM1602_IIC3.SDA
  N2: Part1.A5/SCL, LCM1602_IIC3.SCL
  N3: Part1.D9_PWM, DS3.DQ, R15.Pin_0
  N4: Part1.D10_PWM/SS, DS2.DQ, R18.Pin_0
  N5: Part1.D11_PWM/MOSI, S3.Pin_3, S3.Pin_4, R19.Pin_0
  N6: Part1.D3_PWM, R3.leg2
  N7: Part1.D4, R3.leg1
  N8: Part1.D5_PWM, Q2.gate, R9.Pin_1
  N9: Part1.D6_PWM, Q3.gate, R8.Pin_1
  N10: Part1.D7, Q1.gate, R7.Pin_1
  VDD: Part1.5V, DS2.VDD, S3.Pin_1, S3.Pin_2, DS3.VDD, LCM1602_IIC3.VCC, R15.Pin_1, R18.Pin_1
  GND: Part1.GND, Q1.source, Q3.source, DS2.GND, R3.wiper, Q2.source, R7.Pin_0, R8.Pin_0, R9.Pin_0, DS3.GND, J4.GNDBREAK, LCM1602_IIC3.GND, R19.Pin_1
  N11: Part1.VIN, D1.cathode, M4.pin_1, U3.O, R16.Pin_0, R17.Pin_0
  N12: Q1.drain, R17.Pin_1
  N13: Q3.drain, R16.Pin_1
  N14: Q2.drain, D1.anode
  N15: J4.GND, U3.P
  VSS: LCM1602_IIC3.VSS, LCD2.VSS
  VDD_2: LCM1602_IIC3.VDD, LCD2.VDD
  N16: LCM1602_IIC3.V0, LCD2.V0
  N17: LCM1602_IIC3.RS, LCD2.RS
  N18: LCM1602_IIC3.RW, LCD2.R/W
  N19: LCM1602_IIC3.E, LCD2.E
  N20: LCM1602_IIC3.D0, LCD2.DB0
  N21: LCM1602_IIC3.D1, LCD2.DB1
  N22: LCM1602_IIC3.D2, LCD2.DB2
  N23: LCM1602_IIC3.D3, LCD2.DB3
  N24: LCM1602_IIC3.D4, LCD2.DB4
  N25: LCM1602_IIC3.D5, LCD2.DB5
  N26: LCM1602_IIC3.D6, LCD2.DB6
  N27: LCM1602_IIC3.D7, LCD2.DB7
  N28: LCM1602_IIC3.A, LCD2.LED+
  N29: LCM1602_IIC3.K, LCD2.LED-
  N30: LCM1602_IIC3.LED_A, LCM1602_IIC3.LED_B

notes:
  thermo sensors
  + 4.7K ohm R
  Ceramic (220ohm) resistors
  Fan
  12V power Supply
  Rotary encoder
  10K ohm R +
  Push Button
  Mosfets
  10K ohm R

custom parts:
  LCM1602 IIC: I2C-Module to use a 1602 or 2004 LCD on with the wire.h libory Serial LCD Modul
