# Fritzing sketch Thermocycler-Fritzing (saved by Fritzing 0.9.2b)
breadboards: 2

parts:
  S1_Power_Switch = Pushbutton [package=THT]
  Power_plug1_-_12V = Power plug
  U1 = mystery part, 4 pins [chip_label=I2C spacing=300mil]
  R1_-_Rotary_encoder = Rotary Potentiometer (Small) [maximum_resistance=100kΩ package=THT]
  LCD1 = LCD screen  # not connected
  Arduino1 = Arduino Uno (Rev3)
  S1 = Pushbutton [package="[THT]"]
  R1 = Resistor [tolerance=±5% resistance=1k package=THT]
  R2 = Resistor [tolerance=±5% resistance=10k package=THT]
  R3 = Resistor [tolerance=±5% resistance=10 power=7W package=THT]
  R4 = Resistor [tolerance=±5% resistance=10 power=7W package=THT]
  R5 = Resistor [tolerance=±5% resistance=10 power=7W package=THT]
  M1 = DC Motor
  Q1 = Basic FET N-Channel [package="TO220 [THT]"]
  Q2 = Basic FET N-Channel [package="TO220 [THT]"]
  R6 = Resistor [tolerance=±5% resistance=10k package=THT]
  R7 = Temperature Sensor (Thermistor) [thermistor_type=NTC package=THT]
  R8 = Resistor [tolerance=±5% resistance=10k package="2010 [SMD]"]
  D1 = Rectifier Diode [part_number=1N4001 package="300 mil [THT]"]

nets:
  N1: S1_Power_Switch.leg0, Power_plug1_-_12V.VCC
  N2: S1_Power_Switch.leg1, Arduino1.VIN, R3.Pin_0, R4.Pin_0, R5.Pin_0, M1.pin_1, D1.cathode
  GND: Power_plug1_-_12V.GND, U1.pin4, R1_-_Rotary_encoder.wiper, Arduino1.GND, R1.Pin_1, R2.Pin_1, Q1.source, Q2.source, R6.Pin_1, R7.pin_1
  N3: U1.pin1, Arduino1.A5/SCL
  N4: U1.pin2, Arduino1.A4/SDA
  N5: U1.pin3, Arduino1.5V, S1.Pin_3, S1.Pin_4, R8.Pin_1
  N6: R1_-_Rotary_encoder.leg1, Arduino1.D2
  N7: R1_-_Rotary_encoder.leg2, Arduino1.D3_PWM
  N8: Arduino1.A0, R7.pin_0, R8.Pin_0
  N9: Arduino1.D11_PWM/MOSI, S1.Pin_1, S1.Pin_2, R1.Pin_0
  N10: Arduino1.D5_PWM, R2.Pin_0, Q1.gate
  N11: Arduino1.D6_PWM, Q2.gate, R6.Pin_0
  N12: R3.Pin_1, R4.Pin_1, R5.Pin_1, Q1.drain
  N13: M1.pin_2, Q2.drain, D1.anode

notes:
  LCD I2C interface
  SCL - A5
  SDA - A4
  Vcc
  Gnd
  Rotary Encoder
  Power switch
  12V power supply
  Push Button
  12 V Power Supply
  Power Switch
  Push button
  Rotary encoder
  The LCD has an I2C interface
  Power Resistors
  Fan
  The Arduino converts the 12V to 5V
  Temperature sensor
